# Fritzing sketch BaseUnit_Test_Board_Ver3_0 (saved by Fritzing 0.9.3b)

parts:
  R1 = Resistor [tolerance=±5% resistance=10k package=THT]
  R2 = Resistor [tolerance=±5% resistance=10k package=THT]
  R3 = Resistor [tolerance=±5% resistance=10k package=THT]
  R4 = Resistor [tolerance=±5% resistance=10k package=THT]
  R5 = Resistor [tolerance=±5% resistance=1k package=THT]
  LED1 = LED - 5mm [color="Red (633nm)" package="5 mm [THT]"]
  S2 = Pushbutton [package="[SMD]"]
  S3 = Pushbutton [package="[SMD]"]
  S4 = Pushbutton [package="[SMD]"]
  S5 = Pushbutton [package="[SMD]"]
  J17 = 2Pin header connector (female) [package=THT]
  J18 = 2Pin header connector (female) [package=THT]
  Mod2 = Raspberry Pi Pico
  OLED_I2C2 = OLED 128x64 I2C Monochrome Display
  R6 = Resistor [tolerance=±5% resistance=10k package=THT]
  S6 = Pushbutton [package="[SMD]"]
  D1 = Rectifier Diode 10A [part_number=1N5819]
  LED2 = LED - 5mm [color="Red (633nm)" package="5 mm [THT]"]
  LED4 = LED - 5mm [color="Red (633nm)" package="5 mm [THT]"]
  LED5 = LED - 5mm [color="Red (633nm)" package="5 mm [THT]"]
  R7 = Resistor [tolerance=±5% resistance=1k package=THT]
  R10 = Resistor [tolerance=±5% resistance=1k package=THT]
  R11 = Resistor [tolerance=±5% resistance=1k package=THT]
  J19 = 2Pin header connector (female) [package=THT]  # not connected
  J20 = 2Pin header connector (female) [package=THT]  # not connected

nets:
  N1: R1.Pin_0, R2.Pin_0, R3.Pin_0, R4.Pin_0, Mod2.pin_36, R6.Pin_0, D1.anode
  N2: R1.Pin_1, S5.Pin_3, S5.Pin_4, Mod2.pin_16
  N3: R2.Pin_1, S2.Pin_3, S2.Pin_4, Mod2.pin_20
  N4: R3.Pin_1, S3.Pin_3, S3.Pin_4, Mod2.pin_19
  N5: R4.Pin_1, S4.Pin_3, S4.Pin_4, Mod2.pin_17
  N6: R5.Pin_0, Mod2.pin_21
  N7: LED1.cathode, S2.Pin_1, S2.Pin_2, S3.Pin_1, S3.Pin_2, S4.Pin_1, S4.Pin_2, S5.Pin_1, J18.Pin1, Mod2.pin_13, Mod2.pin_23, Mod2.pin_28, Mod2.pin_33, Mod2.pin_38, Mod2.pin_42, OLED_I2C2.GND, S6.Pin_1, S6.Pin_2, LED2.cathode, LED4.cathode, LED5.cathode
  N8: J17.Pin1, Mod2.pin_11
  N9: J17.Pin2, Mod2.pin_12
  N10: J18.Pin2, D1.cathode
  N11: Mod2.pin_22, R11.Pin_0
  N12: Mod2.pin_24, OLED_I2C2.SDA
  N13: Mod2.pin_25, OLED_I2C2.SCK
  N14: Mod2.pin_26, R7.Pin_0
  N15: Mod2.pin_27, R10.Pin_0
  N16: Mod2.pin_40, OLED_I2C2.VDD
  N17: R6.Pin_1, S6.Pin_4

notes:
  SCL
  SDA
  0V
  +5V
  TX- 1
  RX- 1
  +3V3
  OLED I2C - 1
  SDA- GP18
  SCL - GP19
  UART - 1
  TX- GP8
  RX - GP9
  UART Commands
  GP11 - 'Right'
  GP12 - 'Backward'
  GP13 - 'Stop'
  GP14 - 'Forward'
  GP15 - 'Left'
  Left
  Right
  Forward
  Backward
  Stop
  1N5819
  Rear Left rl=GP21
  Rear Right rr=GP20
  Front Left fl=GP17
  Front Right fr=GP16
  IR Sensors (from base unit)
  RL- GP21
  RR- GP20
  FL- GP17
  FR- GP16
  BaseUnit Test Board Ver3.0
  RX- 2
  TX- 2
  Simulates the operation of the
  Main AI Processor controller
  Testing the UART Communications
  Remote Base Unit UAR

custom parts:
  2Pin header connector (female): 2Pin header connector (female) This part represents the header plug
  Raspberry Pi Pico: Raspberry Pi Pico. Based around the RP2040 microcontroller the Pico is a low cost microcontroller device bringing Raspberry Pi quality, cost, and easy of use to the microcontroller space. Jan 2021, Split part in to two versions: tht (this one) and SMD. This one will drill holes for a .1 in header in pcb to allow plugging in the module as well as providing pads to solder the module to the top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
